// Logisim project 8-BIT ALU PROJECT.circ as structural Verilog: 8 circuits, main circuit main
module main (
  input  [1:0] _10___OR,
  input  [7:0] in_2,
  input  [7:0] in_3,
  output [7:0] out_4,
  output out_5
);

  wire double_dabble_1_out_9, double_dabble_1_out_10, double_dabble_1_out_11, double_dabble_1_out_12,
       double_dabble_1_out_13, double_dabble_1_out_14, double_dabble_1_out_15, double_dabble_1_out_16,
       double_dabble_1_out_17, double_dabble_1_out_18, double_dabble_1_out_19, double_dabble_1_out_20,
       n7447_1_a_2, n7447_1_b_2, n7447_1_c_2, n7447_1_d_2, n7447_1_e, n7447_1_f, n7447_1_g, n7447_2_a_2,
       n7447_2_b_2, n7447_2_c_2, n7447_2_d_2, n7447_2_e, n7447_2_f, n7447_2_g, n7447_3_a_2, n7447_3_b_2,
       n7447_3_c_2, n7447_3_d_2, n7447_3_e, n7447_3_f, n7447_3_g;
  wire [7:0] add_sub_1_out_3, and_1_out_3, or_1_out_3;

  ADD___SUB add_sub_1 (.A(in_2), .B(in_3), .out_3(add_sub_1_out_3), .Cout(out_5));
  AND and_1 (.A(in_2), .B(in_3), .out_3(and_1_out_3));
  OR or_1 (.A(in_2), .B(in_3), .out_3(or_1_out_3));
  Multiplexer #(.select(2), .width(8), .enable("false")) multiplexer_1 (
    .in0(add_sub_1_out_3), .in1(and_1_out_3), .in2(or_1_out_3), .in3(or_1_out_3), .out(out_4), .sel(_10___OR));
  Double_Dabble double_dabble_1 (
    .in_1(out_4[7]), .in_2(out_4[6]), .in_3(out_4[5]), .in_4(out_4[4]), .in_5(out_4[3]), .in_6(out_4[2]),
    .in_7(out_4[1]), .in_8(out_4[0]), .out_9(double_dabble_1_out_9), .out_10(double_dabble_1_out_10),
    .out_11(double_dabble_1_out_11), .out_12(double_dabble_1_out_12), .out_13(double_dabble_1_out_13),
    .out_14(double_dabble_1_out_14), .out_15(double_dabble_1_out_15), .out_16(double_dabble_1_out_16),
    .out_17(double_dabble_1_out_17), .out_18(double_dabble_1_out_18), .out_19(double_dabble_1_out_19),
    .out_20(double_dabble_1_out_20));
  _7447 u_7447_1 (
    .D(double_dabble_1_out_9), .C(double_dabble_1_out_10), .B(double_dabble_1_out_11),
    .A(double_dabble_1_out_12), .a_2(n7447_1_a_2), .b_2(n7447_1_b_2), .c_2(n7447_1_c_2), .d_2(n7447_1_d_2),
    .e(n7447_1_e), .f(n7447_1_f), .g(n7447_1_g));
  _7447 u_7447_2 (
    .D(double_dabble_1_out_13), .C(double_dabble_1_out_14), .B(double_dabble_1_out_15),
    .A(double_dabble_1_out_16), .a_2(n7447_2_a_2), .b_2(n7447_2_b_2), .c_2(n7447_2_c_2), .d_2(n7447_2_d_2),
    .e(n7447_2_e), .f(n7447_2_f), .g(n7447_2_g));
  _7447 u_7447_3 (
    .D(double_dabble_1_out_17), .C(double_dabble_1_out_18), .B(double_dabble_1_out_19),
    .A(double_dabble_1_out_20), .a_2(n7447_3_a_2), .b_2(n7447_3_b_2), .c_2(n7447_3_c_2), .d_2(n7447_3_d_2),
    .e(n7447_3_e), .f(n7447_3_f), .g(n7447_3_g));
  _7_Segment_Display u_7_segment_display_1 (
    .g(n7447_2_g), .f(n7447_2_f), .a(n7447_2_a_2), .b(n7447_2_b_2), .e(n7447_2_e), .d(n7447_2_d_2),
    .c(n7447_2_c_2));  // open: dp
  _7_Segment_Display u_7_segment_display_2 (
    .g(n7447_1_g), .f(n7447_1_f), .a(n7447_1_a_2), .b(n7447_1_b_2), .e(n7447_1_e), .d(n7447_1_d_2),
    .c(n7447_1_c_2));  // open: dp
  _7_Segment_Display u_7_segment_display_3 (
    .g(n7447_3_g), .f(n7447_3_f), .a(n7447_3_a_2), .b(n7447_3_b_2), .e(n7447_3_e), .d(n7447_3_d_2),
    .c(n7447_3_c_2));  // open: dp

  // Notes on the sheet:
  //   ADD / SUB
  //   AND
  //   OR
  //   00 - ADD / SUB 
  //   01 - AND 
endmodule

module Full_Adder (
  input  A,
  input  B,
  input  Cin,
  output Sum,
  output Cout
);

  wire and_1_out, and_2_out, xor_1_out;

  xor xor_1 (xor_1_out, A, B);
  and and_1 (and_1_out, A, B);
  and and_2 (and_2_out, xor_1_out, Cin);
  xor xor_2 (Sum, xor_1_out, Cin);
  or or_1 (Cout, and_2_out, and_1_out);
endmodule

module ADD___SUB (
  input  [7:0] A,
  input  [7:0] B,
  output [7:0] out_3,
  output Cout
);

  wire full_adder_1_cout, full_adder_2_cout, full_adder_3_cout, full_adder_4_cout, full_adder_5_cout,
       full_adder_6_cout, full_adder_7_cout;

  Full_Adder full_adder_1 (.A(A[0]), .B(B[0]), .Cin(1'b0), .Sum(out_3[0]), .Cout(full_adder_1_cout));
  Full_Adder full_adder_2 (.A(A[1]), .B(B[1]), .Cin(full_adder_1_cout), .Sum(out_3[1]), .Cout(full_adder_2_cout));
  Full_Adder full_adder_3 (.A(A[2]), .B(B[2]), .Cin(full_adder_2_cout), .Sum(out_3[2]), .Cout(full_adder_3_cout));
  Full_Adder full_adder_4 (.A(A[3]), .B(B[3]), .Cin(full_adder_3_cout), .Sum(out_3[3]), .Cout(full_adder_4_cout));
  Full_Adder full_adder_5 (.A(A[4]), .B(B[4]), .Cin(full_adder_4_cout), .Sum(out_3[4]), .Cout(full_adder_5_cout));
  Full_Adder full_adder_6 (.A(A[5]), .B(B[5]), .Cin(full_adder_5_cout), .Sum(out_3[5]), .Cout(full_adder_6_cout));
  Full_Adder full_adder_7 (.A(A[6]), .B(B[6]), .Cin(full_adder_6_cout), .Sum(out_3[6]), .Cout(full_adder_7_cout));
  Full_Adder full_adder_8 (.A(A[7]), .B(B[7]), .Cin(full_adder_7_cout), .Sum(out_3[7]), .Cout(Cout));
endmodule

module AND (
  input  [7:0] A,
  input  [7:0] B,
  output [7:0] out_3
);

  assign out_3 = A & B;  // AND_Gate and_1, 8 bits wide
endmodule

module OR (
  input  [7:0] A,
  input  [7:0] B,
  output [7:0] out_3
);

  assign out_3 = A | B;  // OR_Gate or_1, 8 bits wide
endmodule

module _7447 (
  input  D,
  input  C,
  input  B,
  input  A,
  output a_2,
  output b_2,
  output c_2,
  output d_2,
  output e,
  output f,
  output g
);

  wire nand_1_out, nand_2_out, nand_3_out, nand_4_out, nand_5_out, nand_6_out, nand_7_out, nand_8_out,
       nand_9_out, nand_10_out, nand_11_out, nand_12_out, nand_13_out, nand_14_out, nand_15_out, nand_16_out,
       nand_17_out, nand_18_out, nand_19_out, nand_20_out, nand_21_out, nand_22_out, nand_23_out,
       nand_24_out, nand_25_out, nand_26_out, nand_27_out, nand_28_out, nand_29_out, nand_30_out,
       nand_31_out, nand_32_out, nand_33_out, nand_34_out, nand_35_out, nand_36_out, nand_37_out,
       nand_38_out, nand_39_out, nand_40_out, nand_41_out, nand_42_out, nand_43_out, nand_44_out,
       nand_45_out, nand_46_out, nand_47_out, nand_48_out, nand_49_out, nand_50_out, nand_51_out,
       nand_52_out, nand_53_out, nand_54_out, nand_55_out, nand_56_out, nand_57_out, nand_58_out,
       nand_59_out, nand_60_out, nand_61_out, nand_62_out, nand_63_out, nand_64_out, nand_65_out,
       nand_66_out, nand_67_out, nand_68_out, nand_69_out, nand_70_out, nand_71_out, nand_72_out,
       nand_73_out, nand_74_out, nand_75_out, nand_76_out, nand_77_out, nand_78_out, nand_79_out,
       nand_80_out, nand_81_out, nand_82_out, nand_83_out, nand_84_out, nand_85_out, nand_86_out,
       nand_87_out, nand_88_out, nand_89_out, nand_90_out, nand_91_out, nand_92_out, nand_93_out,
       nand_94_out, nand_95_out, nand_96_out, nand_97_out, nand_98_out, nand_99_out, nand_100_out,
       nand_101_out, nand_102_out, nand_103_out, nand_104_out, nand_106_out, nand_107_out, nand_108_out,
       nand_109_out, nand_110_out, nand_111_out, nand_112_out, nand_113_out, nand_114_out, nand_115_out,
       nand_116_out, nand_117_out, nand_118_out, nand_119_out, nand_120_out, nand_121_out, nand_122_out,
       nand_123_out, nand_124_out, nand_125_out, nand_126_out, nand_127_out, nand_128_out, nand_129_out,
       nand_130_out, nand_131_out, nand_132_out, nand_133_out, nand_134_out, nand_136_out, nand_137_out,
       nand_138_out, nand_139_out, nand_141_out, nand_142_out, nand_143_out, nand_144_out, nand_145_out,
       nand_146_out, nand_147_out, nand_148_out;

  nand nand_1 (nand_1_out, C, C);
  nand nand_2 (nand_2_out, D, D);
  nand nand_3 (nand_3_out, B, B);
  nand nand_4 (nand_4_out, D, D);
  nand nand_5 (nand_5_out, B, B);
  nand nand_6 (nand_6_out, D, D);
  nand nand_7 (nand_7_out, D, D);
  nand nand_8 (nand_8_out, C, C);
  nand nand_9 (nand_9_out, C, C);
  nand nand_10 (nand_10_out, C, C);
  nand nand_11 (nand_11_out, A, A);
  nand nand_12 (nand_12_out, A, A);
  nand nand_13 (nand_13_out, D, D);
  nand nand_14 (nand_14_out, C, C);
  nand nand_15 (nand_15_out, A, A);
  nand nand_16 (nand_16_out, D, D);
  nand nand_17 (nand_17_out, D, nand_1_out);
  nand nand_18 (nand_18_out, nand_2_out, nand_3_out);
  nand nand_19 (nand_19_out, nand_4_out, nand_5_out);
  nand nand_20 (nand_20_out, nand_6_out, A);
  nand nand_21 (nand_21_out, nand_7_out, nand_8_out);
  nand nand_22 (nand_22_out, nand_9_out, B);
  nand nand_23 (nand_23_out, nand_10_out, nand_11_out);
  nand nand_24 (nand_24_out, B, nand_12_out);
  nand nand_25 (nand_25_out, D, B);
  nand nand_26 (nand_26_out, D, C);
  nand nand_27 (nand_27_out, nand_13_out, C);
  nand nand_28 (nand_28_out, nand_14_out, B);
  nand nand_29 (nand_29_out, B, nand_15_out);
  nand nand_30 (nand_30_out, nand_16_out, C);
  nand nand_31 (nand_31_out, C, C);
  nand nand_32 (nand_32_out, A, A);
  nand nand_33 (nand_33_out, D, D);
  nand nand_34 (nand_34_out, D, D);
  nand nand_35 (nand_35_out, nand_17_out, nand_17_out);
  nand nand_36 (nand_36_out, B, B);
  nand nand_37 (nand_37_out, D, D);
  nand nand_38 (nand_38_out, C, C);
  nand nand_39 (nand_39_out, nand_18_out, nand_18_out);
  nand nand_40 (nand_40_out, A, A);
  nand nand_41 (nand_41_out, D, D);
  nand nand_42 (nand_42_out, B, B);
  nand nand_43 (nand_43_out, nand_19_out, nand_20_out);
  nand nand_44 (nand_44_out, B, B);
  nand nand_45 (nand_45_out, D, D);
  nand nand_46 (nand_46_out, C, C);
  nand nand_47 (nand_47_out, nand_21_out, nand_21_out);
  nand nand_48 (nand_48_out, A, A);
  nand nand_49 (nand_49_out, nand_22_out, nand_22_out);
  nand nand_50 (nand_50_out, B, B);
  nand nand_51 (nand_51_out, B, B);
  nand nand_52 (nand_52_out, nand_23_out, nand_24_out);
  nand nand_53 (nand_53_out, nand_25_out, nand_26_out);
  nand nand_54 (nand_54_out, B, B);
  nand nand_55 (nand_55_out, A, A);
  nand nand_56 (nand_56_out, nand_27_out, nand_27_out);
  nand nand_57 (nand_57_out, B, B);
  nand nand_58 (nand_58_out, nand_28_out, nand_29_out);
  nand nand_59 (nand_59_out, nand_30_out, nand_30_out);
  nand nand_60 (nand_60_out, B, B);
  nand nand_61 (nand_61_out, C, C);
  nand nand_62 (nand_62_out, nand_31_out, nand_32_out);
  nand nand_63 (nand_63_out, nand_33_out, B);
  nand nand_64 (nand_64_out, nand_34_out, C);
  nand nand_65 (nand_65_out, C, B);
  nand nand_66 (nand_66_out, nand_35_out, nand_36_out);
  nand nand_67 (nand_67_out, nand_37_out, nand_38_out);
  nand nand_68 (nand_68_out, nand_39_out, nand_40_out);
  nand nand_69 (nand_69_out, nand_41_out, B);
  nand nand_70 (nand_70_out, D, nand_42_out);
  nand nand_71 (nand_71_out, nand_43_out, nand_43_out);
  nand nand_72 (nand_72_out, nand_44_out, A);
  nand nand_73 (nand_73_out, nand_45_out, C);
  nand nand_74 (nand_74_out, D, nand_46_out);
  nand nand_75 (nand_75_out, nand_47_out, nand_48_out);
  nand nand_76 (nand_76_out, nand_49_out, A);
  nand nand_77 (nand_77_out, C, nand_50_out);
  nand nand_78 (nand_78_out, C, B);
  nand nand_79 (nand_79_out, D, nand_51_out);
  nand nand_80 (nand_80_out, nand_52_out, nand_52_out);
  nand nand_81 (nand_81_out, nand_53_out, nand_53_out);
  nand nand_82 (nand_82_out, nand_54_out, nand_55_out);
  nand nand_83 (nand_83_out, nand_56_out, nand_57_out);
  nand nand_84 (nand_84_out, nand_58_out, nand_58_out);
  nand nand_85 (nand_85_out, nand_59_out, nand_60_out);
  nand nand_86 (nand_86_out, D, nand_61_out);
  nand nand_87 (nand_87_out, D, A);
  nand nand_88 (nand_88_out, nand_62_out, nand_63_out);
  nand nand_89 (nand_89_out, nand_64_out, nand_64_out);
  nand nand_90 (nand_90_out, nand_65_out, nand_66_out);
  nand nand_91 (nand_91_out, A, A);
  nand nand_92 (nand_92_out, nand_67_out, nand_68_out);
  nand nand_93 (nand_93_out, C, C);
  nand nand_94 (nand_94_out, A, A);
  nand nand_95 (nand_95_out, nand_69_out, nand_69_out);
  nand nand_96 (nand_96_out, nand_70_out, nand_70_out);
  nand nand_97 (nand_97_out, nand_71_out, nand_72_out);
  nand nand_98 (nand_98_out, nand_73_out, nand_74_out);
  nand nand_99 (nand_99_out, nand_75_out, nand_76_out);
  nand nand_100 (nand_100_out, nand_77_out, nand_77_out);
  nand nand_101 (nand_101_out, nand_78_out, nand_78_out);
  nand nand_102 (nand_102_out, A, A);
  nand nand_103 (nand_103_out, nand_79_out, nand_79_out);
  nand nand_104 (nand_104_out, A, A);
  nand nand_105 (e, nand_80_out, nand_81_out);
  nand nand_106 (nand_106_out, nand_82_out, nand_83_out);
  nand nand_107 (nand_107_out, A, A);
  nand nand_108 (nand_108_out, C, C);
  nand nand_109 (nand_109_out, nand_84_out, nand_85_out);
  nand nand_110 (nand_110_out, nand_86_out, nand_87_out);
  nand nand_111 (nand_111_out, nand_88_out, nand_88_out);
  nand nand_112 (nand_112_out, nand_89_out, A);
  nand nand_113 (nand_113_out, nand_90_out, nand_90_out);
  nand nand_114 (nand_114_out, D, nand_91_out);
  nand nand_115 (nand_115_out, nand_92_out, nand_92_out);
  nand nand_116 (nand_116_out, nand_93_out, nand_94_out);
  nand nand_117 (nand_117_out, nand_95_out, A);
  nand nand_118 (nand_118_out, nand_96_out, A);
  nand nand_119 (nand_119_out, nand_97_out, nand_97_out);
  nand nand_120 (nand_120_out, nand_98_out, nand_98_out);
  nand nand_121 (nand_121_out, nand_99_out, nand_99_out);
  nand nand_122 (nand_122_out, nand_100_out, A);
  nand nand_123 (nand_123_out, nand_101_out, nand_102_out);
  nand nand_124 (nand_124_out, nand_103_out, nand_104_out);
  nand nand_125 (nand_125_out, nand_106_out, nand_106_out);
  nand nand_126 (nand_126_out, C, nand_107_out);
  nand nand_127 (nand_127_out, D, nand_108_out);
  nand nand_128 (nand_128_out, D, B);
  nand nand_129 (nand_129_out, nand_109_out, nand_109_out);
  nand nand_130 (nand_130_out, nand_110_out, nand_110_out);
  nand nand_131 (nand_131_out, nand_111_out, nand_112_out);
  nand nand_132 (nand_132_out, nand_113_out, nand_114_out);
  nand nand_133 (nand_133_out, nand_115_out, nand_116_out);
  nand nand_134 (nand_134_out, nand_117_out, nand_118_out);
  nand nand_135 (c_2, nand_119_out, nand_120_out);
  nand nand_136 (nand_136_out, nand_121_out, nand_122_out);
  nand nand_137 (nand_137_out, nand_123_out, nand_124_out);
  nand nand_138 (nand_138_out, nand_125_out, nand_126_out);
  nand nand_139 (nand_139_out, nand_127_out, nand_128_out);
  nand nand_140 (g, nand_129_out, nand_130_out);
  nand nand_141 (nand_141_out, nand_131_out, nand_131_out);
  nand nand_142 (nand_142_out, nand_132_out, nand_132_out);
  nand nand_143 (nand_143_out, nand_133_out, nand_133_out);
  nand nand_144 (nand_144_out, nand_134_out, nand_134_out);
  nand nand_145 (nand_145_out, nand_136_out, nand_136_out);
  nand nand_146 (nand_146_out, nand_137_out, nand_137_out);
  nand nand_147 (nand_147_out, nand_138_out, nand_138_out);
  nand nand_148 (nand_148_out, nand_139_out, nand_139_out);
  nand nand_149 (a_2, nand_141_out, nand_142_out);
  nand nand_150 (b_2, nand_143_out, nand_144_out);
  nand nand_151 (d_2, nand_145_out, nand_146_out);
  nand nand_152 (f, nand_147_out, nand_148_out);
endmodule

module Dabble (
  input  in_1,
  input  in_2,
  input  in_3,
  input  in_4,
  output out_5,
  output out_6,
  output out_7,
  output out_8
);

  wire nor_1_out, nor_2_out, or_1_out, xor_1_out, xor_2_out;

  xor xor_1 (xor_1_out, in_4, in_1);
  nor nor_1 (nor_1_out, in_1, in_2);
  xor xor_2 (xor_2_out, in_1, in_3);
  nor nor_2 (nor_2_out, xor_1_out, xor_2_out);
  nor nor_3 (out_5, nor_2_out, nor_1_out);
  or or_1 (or_1_out, xor_1_out, nor_1_out);
  nor nor_4 (out_6, or_1_out, in_3);
  and and_1 (out_7, or_1_out, xor_2_out);
  xor xor_3 (out_8, out_5, in_4);
endmodule

module Double_Dabble (
  input  in_1,
  input  in_2,
  input  in_3,
  input  in_4,
  input  in_5,
  input  in_6,
  input  in_7,
  input  in_8,
  output out_9,
  output out_10,
  output out_11,
  output out_12,
  output out_13,
  output out_14,
  output out_15,
  output out_16,
  output out_17,
  output out_18,
  output out_19,
  output out_20
);

  wire dabble_1_out_5, dabble_1_out_6, dabble_1_out_7, dabble_1_out_8, dabble_2_out_5, dabble_2_out_6,
       dabble_2_out_7, dabble_2_out_8, dabble_3_out_5, dabble_3_out_6, dabble_3_out_7, dabble_3_out_8,
       dabble_4_out_5, dabble_4_out_6, dabble_4_out_7, dabble_4_out_8, dabble_6_out_6, dabble_6_out_7,
       dabble_6_out_8;

  Dabble dabble_1 (
    .in_1(1'b0), .in_2(in_1), .in_3(in_2), .in_4(in_3), .out_5(dabble_1_out_5), .out_6(dabble_1_out_6),
    .out_7(dabble_1_out_7), .out_8(dabble_1_out_8));
  Dabble dabble_2 (
    .in_1(dabble_1_out_6), .in_2(dabble_1_out_7), .in_3(dabble_1_out_8), .in_4(in_4), .out_5(dabble_2_out_5),
    .out_6(dabble_2_out_6), .out_7(dabble_2_out_7), .out_8(dabble_2_out_8));
  Dabble dabble_3 (
    .in_1(dabble_2_out_6), .in_2(dabble_2_out_7), .in_3(dabble_2_out_8), .in_4(in_5), .out_5(dabble_3_out_5),
    .out_6(dabble_3_out_6), .out_7(dabble_3_out_7), .out_8(dabble_3_out_8));
  Dabble dabble_4 (
    .in_1(dabble_3_out_6), .in_2(dabble_3_out_7), .in_3(dabble_3_out_8), .in_4(in_6), .out_5(dabble_4_out_5),
    .out_6(dabble_4_out_6), .out_7(dabble_4_out_7), .out_8(dabble_4_out_8));
  Dabble dabble_5 (
    .in_1(dabble_4_out_6), .in_2(dabble_4_out_7), .in_3(dabble_4_out_8), .in_4(in_7), .out_5(out_16),
    .out_6(out_17), .out_7(out_18), .out_8(out_19));
  Dabble dabble_6 (
    .in_1(1'b0), .in_2(dabble_1_out_5), .in_3(dabble_2_out_5), .in_4(dabble_3_out_5), .out_5(out_11),
    .out_6(dabble_6_out_6), .out_7(dabble_6_out_7), .out_8(dabble_6_out_8));
  Dabble dabble_7 (
    .in_1(dabble_6_out_6), .in_2(dabble_6_out_7), .in_3(dabble_6_out_8), .in_4(dabble_4_out_5),
    .out_5(out_12), .out_6(out_13), .out_7(out_14), .out_8(out_15));

  assign out_9 = 1'b0;
  assign out_10 = 1'b0;
  assign out_20 = in_8;
endmodule
